# Fritzing sketch strongman stapler (saved by Fritzing 0.9.0b)
breadboards: 1

parts:
  TRINKET1 = Trinket 5V
  S1 = Pushbutton [package="[THT]"]
  J1 = Basic Force Sensing Resistor (FSR) [package=THT]
  R1 = Resistor [tolerance=±5% resistance=1k package=THT]
  R2 = Resistor [tolerance=±5% resistance=1k package=THT]
  NEOPIXEL1 = Neopixel Strip -- White (60/m)
  Power_plug1 = Power plug  # not connected

nets:
  N1: TRINKET1.no_name_yet#1, S1.Pin_1, S1.Pin_2, R1.Pin_0, NEOPIXEL1.DI
  N2: TRINKET1.no_name_yet#2, NEOPIXEL1.GND
  N3: TRINKET1.no_name_yet#4, S1.Pin_3, S1.Pin_4, R1.Pin_1
  N4: TRINKET1.no_name_yet#7, R2.Pin_1
  N5: TRINKET1.no_name_yet#9, NEOPIXEL1.+5V
  N6: J1.pin_1, R2.Pin_0

custom parts:
  Trinket 5V: Adafruit Trinket 5V
  Neopixel Strip -- White (60/m): Neopixel Strip, White, 60 pixels per meter.
